# Fritzing sketch ArduinoCircuit (saved by Fritzing 0.9.3b)
breadboards: 1

parts:
  Part1 = Arduino Uno (Rev3)
  T1 = LM35 Temperature Sensor [package="TO92 [THT]"]
  RHT1 = Humidity and Temperature Sensor RHT03
  R1 = Resistor [tolerance=±5% resistance=1k package=THT]
  R2 = PHOTOCELL [package=photocell-kit]
  R3 = Resistor [tolerance=±5% resistance=1k package=THT]
  hc-sr1 = hc-sr04
  LED1 = smd LED [color="Red (633nm)" package="1206 [SMD]"]
  R4 = Resistor [tolerance=±5% resistance=1k package=THT]

nets:
  GND: Part1.A0, Part1.GND, T1.GND, RHT1.GND_2, R3.Pin_1, hc-sr1.GND, LED1.cathode
  N1: Part1.A1, T1.Vout
  N2: Part1.D10_PWM/SS, RHT1.Data-signal, R1.Pin_1
  N3: Part1.D4, R4.Pin_0
  N4: Part1.D6_PWM, hc-sr1.Echo
  N5: Part1.D7, hc-sr1.Trig
  VCC: Part1.5V, T1.+Vs, RHT1.Vcc, R1.Pin_0, R2.P$1, hc-sr1.VCC
  N6: R2.P$2, R3.Pin_0
  N7: LED1.anode, R4.Pin_1
